// Logisim project SR LATCH.circ as structural Verilog: 2 circuits, main circuit main
module main (
);

  // OR_Gate or_1 is placed but not wired
endmodule

module circuit_test (
  input  hi_temp,
  input  low_temp,
  output q,
  output q_prime
);

  wire and_1_out, nor_1_out;

  and and_1 (and_1_out, hi_temp, low_temp);
  nor nor_1 (nor_1_out, low_temp, hi_temp);
  nor nor_2 (q, and_1_out, q_prime);
  nor nor_3 (q_prime, q, nor_1_out);

  // Notes on the sheet:
  //   S
  //   R
endmodule
